# Fritzing sketch piano (saved by Fritzing 1.0.5)
breadboards: 1

parts:
  Part1 = Arduino Uno (Rev3)
  SP1 = SPEAKER [package=pcb_mount_speaker]
  S1 = Pushbutton [package="[THT]"]
  S2 = Pushbutton [package="[THT]"]
  S3 = Pushbutton [package="[THT]"]
  S4 = Pushbutton [package="[THT]"]

nets:
  N1: Part1.D8, S3.Pin_3, S3.Pin_4
  N2: Part1.D9_PWM, S2.Pin_3, S2.Pin_4
  N3: Part1.D10_PWM/SS, S1.Pin_3, S1.Pin_4
  N4: Part1.D11_PWM/MOSI, SP1.-
  N5: Part1.GND, SP1.+, S1.Pin_1, S1.Pin_2, S2.Pin_1, S2.Pin_2, S3.Pin_1, S3.Pin_2, S4.Pin_1, S4.Pin_2
  N6: Part1.D7, S4.Pin_3, S4.Pin_4
